# Fritzing sketch Arduino-Breadboard (saved by Fritzing 0.9.2b)
breadboards: 1

parts:
  Part1 = Arduino Uno (Rev3) - ICSP
  D1 = LTE-302 [package=lte-302]
  R1 = Resistor [tolerance=±5% resistance=470 package="0402 [SMD]"]
  D2 = LTE-302 [package=lte-302]
  R2 = Resistor [tolerance=±5% resistance=470 package="0402 [SMD]"]
  D3 = LTE-302 [package=lte-302]
  R3 = Resistor [tolerance=±5% resistance=470 package="0402 [SMD]"]
  S1 = Pushbutton [package=THT]

nets:
  N1: Part1.GND, R1.Pin_1, R2.Pin_1, R3.Pin_1, S1.leg0
  N2: Part1.D3_PWM, D1.A
  N3: Part1.D5_PWM, D2.A
  N4: Part1.D6_PWM, D3.A
  N5: Part1.D7, S1.leg1
  N6: D1.C, R1.Pin_0
  N7: D2.C, R2.Pin_0
  N8: D3.C, R3.Pin_0
